# Fritzing sketch AgriSensor_Schematics (saved by Fritzing 0.9.10b)
breadboards: 2

parts:
  MH-ET_LIVE_ESP32_DEVKIT1 = MH-ET LIVE ESP32 DEVKIT 38 pins
  T1 = LM34 Temperature Sensor [package="TO92 [THT]"]
  Part1 = Soil Moisture Sensor
  ZS-042_RTC1 = ZS-042 RTC Module
  R1 = Resistor [tolerance=±5% power=0.25 resistance=1k package=THT]
  R2 = Resistor [tolerance=±5% power=0.25 resistance=2.2k part_number=2kohms package=THT]
  M1 = ph-4502c [package=THT]
  M2 = MT3608 Module

nets:
  VCC: MH-ET_LIVE_ESP32_DEVKIT1.3V3, T1.+Vs, Part1.VCC, ZS-042_RTC1.VCC, M2.pin2
  N1: MH-ET_LIVE_ESP32_DEVKIT1.IO34, R1.Pin_0, R2.Pin_0
  N2: MH-ET_LIVE_ESP32_DEVKIT1.IO32, Part1.SIG
  GND: MH-ET_LIVE_ESP32_DEVKIT1.GND#58, T1.GND, Part1.GND, ZS-042_RTC1.GND, R2.Pin_1, M2.pin1
  N3: MH-ET_LIVE_ESP32_DEVKIT1.IO22, ZS-042_RTC1.SCL
  N4: MH-ET_LIVE_ESP32_DEVKIT1.IO21, ZS-042_RTC1.SDA
  N5: MH-ET_LIVE_ESP32_DEVKIT1.IO17, T1.Vout
  N6: R1.Pin_1, M1.pin3
  N7: M1.pin5, M2.pin4
  N8: M1.pin6, M2.pin3

custom parts:
  MH-ET LIVE ESP32 DEVKIT 38 pins: http://mh.nodebb.com/topic/2/mh-et-live-esp32-devkit
  ph-4502c: ph-4502c PH Meter.
  MT3608 Module: MT3608 Boost Converter Module Links: Aerosemi MT3608 2A Step Up Converter datasheet
